# Fritzing sketch wiiproject (saved by Fritzing 0.9.2b)
breadboards: 1

parts:
  Raspberry_Pi_B_rev1 = Raspberry Pi B rev1
  U1 = 74HC595 [package="DIP16 [THT]"]
  U2 = 74HC595 [package="DIP16 [THT]"]
  Disp1 = LBT2088AH [part_number=LBT2088AH]
  R1 = Resistor [tolerance=±5% resistance=330 package=THT]
  R2 = Resistor [tolerance=±5% resistance=330 package=THT]
  R3 = Resistor [tolerance=±5% resistance=330 package=THT]
  R4 = Resistor [tolerance=±5% resistance=330 package=THT]
  R5 = Resistor [tolerance=±5% resistance=330 package=THT]
  R6 = Resistor [tolerance=±5% resistance=330 package=THT]
  R7 = Resistor [tolerance=±5% resistance=330 package=THT]
  R8 = Resistor [tolerance=±5% resistance=330 package=THT]

nets:
  N1: Raspberry_Pi_B_rev1.GND, U1.OE
  N2: Raspberry_Pi_B_rev1.GPIO_23, U2.SH_CP
  N3: Raspberry_Pi_B_rev1.GPIO_17, U1.DS
  N4: Raspberry_Pi_B_rev1.GPIO_18, U2.DS
  N5: Raspberry_Pi_B_rev1.GPIO_21, U1.SH_CP
  N6: Raspberry_Pi_B_rev1.GPIO_22, U1.ST_CP
  N7: Raspberry_Pi_B_rev1.GPIO_4, U1.MR
  N8: Raspberry_Pi_B_rev1.GPIO_24, U2.ST_CP
  N9: U1.Q1, Disp1.pin_6
  N10: U1.Q2, Disp1.pin_16
  N11: U1.Q3, Disp1.pin_4
  N12: U1.Q4, Disp1.pin_9
  N13: U1.Q5, Disp1.pin_15
  N14: U1.Q6, Disp1.pin_10
  N15: U1.Q7, Disp1.pin_13
  N16: U1.Q0, Disp1.pin1
  N17: U2.Q1, R4.Pin_1
  N18: U2.Q3, R2.Pin_1
  N19: U2.Q0, R1.Pin_1
  N20: Disp1.pin2, R7.Pin_0
  N21: Disp1.pin_3, R3.Pin_0
  N22: Disp1.pin_5, R5.Pin_0
  N23: Disp1.pin_7, R4.Pin_0
  N24: Disp1.pin_8, R1.Pin_0
  N25: Disp1.pin_11, R8.Pin_0
  N26: Disp1.pin_12, R6.Pin_0
  N27: Disp1.pin_14, R2.Pin_0
